# Fritzing sketch Untitled Sketch 4 (saved by Fritzing 0.9.3b)
circuit board: 8.46667cm x 5.64444cm
breadboards: 1

parts:
  Raspberry_Pi_1 = Raspberry Pi 3 [part_number=RPI-3-V1.2]
  HC-SR04_Sensor_1 = HC-SR04 Ultrasonic Distance Sensor
  LED1 = LEDs [package=led10mm]
  J1 = Piezo Speaker

nets:
  N1: Raspberry_Pi_1.GPIO2, LED1.A
  N2: Raspberry_Pi_1.GPIO3, J1.pin1
  GND: Raspberry_Pi_1.GND, HC-SR04_Sensor_1.GND, LED1.C, J1.pin2
  N3: Raspberry_Pi_1.GPIO24, HC-SR04_Sensor_1.ECHO
  N4: Raspberry_Pi_1.GPIO18, HC-SR04_Sensor_1.TRIG
  5V: Raspberry_Pi_1.5V, HC-SR04_Sensor_1.VCC
